// Logisim project 4BITADDER.circ as structural Verilog: 1 circuit, main circuit main
module main (
  input  in_1,
  input  in_2,
  input  in_3,
  input  in_4,
  input  in_5,
  input  in_6,
  input  in_7,
  input  in_8,
  input  in_9,
  input  in_10,
  input  in_11,
  input  in_12
);

  wire and_1_out, and_2_out, and_3_out, and_4_out, and_5_out, and_6_out, and_7_out, and_8_out, or_4_out,
       xor_1_out, xor_2_out, xor_3_out, xor_4_out, xor_5_out, xor_6_out, xor_7_out, xor_8_out;

  xor xor_1 (xor_1_out, in_2, in_7);
  and and_1 (and_1_out, in_7, in_2);
  xor xor_2 (xor_2_out, in_3, in_8);
  and and_2 (and_2_out, in_8, in_3);
  xor xor_3 (xor_3_out, in_4, in_9);
  and and_3 (and_3_out, in_9, in_4);
  and and_4 (and_4_out, in_10, in_5);
  xor xor_4 (xor_4_out, in_1, xor_1_out);
  and and_5 (and_5_out, xor_1_out, in_1);
  or or_1 (in_6, and_5_out, and_1_out);
  or or_2 (in_11, and_6_out, and_2_out);
  or or_3 (in_12, and_7_out, and_3_out);
  xor xor_5 (xor_5_out, in_5, in_10);
  or or_4 (or_4_out, and_8_out, and_4_out);
  xor xor_6 (xor_6_out, in_6, xor_2_out);
  and and_6 (and_6_out, xor_2_out, in_6);
  xor xor_7 (xor_7_out, in_11, xor_3_out);
  and and_7 (and_7_out, xor_3_out, in_11);
  xor xor_8 (xor_8_out, in_12, xor_5_out);
  and and_8 (and_8_out, xor_5_out, in_12);
  LED led_1 (.in(xor_4_out));
  LED led_2 (.in(or_4_out));
  LED led_3 (.in(xor_7_out));
  LED led_4 (.in(xor_6_out));
  LED led_5 (.in(xor_8_out));

  // Notes on the sheet:
  //   C
  //   A1
  //   B1
  //   A2
  //   B2
  //   A3
  //   B3
  //   A4
  //   B4
  //   C0
endmodule
